# Fritzing sketch 2x3-custom-keypad-wiring (saved by Fritzing 0.9.3b)
breadboards: 2

parts:
  S1 = Pushbutton [package="[THT]"]
  S2 = Pushbutton [package="[THT]"]
  S3 = Pushbutton [package="[THT]"]
  S4 = Pushbutton [package="[THT]"]
  Part1 = Adafruit Feather HUZZAH ESP8266 [part_number="Adafruit #2821"]
  S5 = Pushbutton [package="[THT]"]
  S6 = Pushbutton [package="[THT]"]
  R1 = Resistor [tolerance=±5% resistance=10k package=THT]
  R2 = Resistor [tolerance=±5% resistance=10k package=THT]
  R3 = Resistor [tolerance=±5% resistance=10k package=THT]
  R4 = Resistor [tolerance=±5% resistance=10k package=THT]
  R5 = Resistor [tolerance=±5% resistance=10k package=THT]
  D1 = Zener Diode [part_number=1N4148 breakdown_voltage=3.6V package="300 mil [THT]"]
  D2 = Zener Diode [part_number=1N4148 breakdown_voltage=3.6V package="300 mil [THT]"]
  D3 = Zener Diode [part_number=1N4148 breakdown_voltage=3.6V package="300 mil [THT]"]
  D4 = Zener Diode [part_number=1N4148 breakdown_voltage=3.6V package="300 mil [THT]"]
  D5 = Zener Diode [part_number=1N4148 breakdown_voltage=3.6V package="300 mil [THT]"]
  D6 = Zener Diode [part_number=1N4148 breakdown_voltage=3.6V package="300 mil [THT]"]
  D7 = Zener Diode [part_number=1N4148 breakdown_voltage=3.6V package="300 mil [THT]"]
  D8 = Zener Diode [part_number=1N4148 breakdown_voltage=3.6V package="300 mil [THT]"]
  D9 = Zener Diode [part_number=1N4148 breakdown_voltage=3.6V package="300 mil [THT]"]
  D10 = Zener Diode [part_number=1N4148 breakdown_voltage=3.6V package="300 mil [THT]"]
  D11 = Zener Diode [part_number=1N4148 breakdown_voltage=3.6V package="300 mil [THT]"]
  D12 = Zener Diode [part_number=1N4148 breakdown_voltage=3.6V package="300 mil [THT]"]

nets:
  N1: S1.Pin_1, S1.Pin_2, D4.anode, D10.anode
  N2: S1.Pin_3, S1.Pin_4, S2.Pin_3, S2.Pin_4, S3.Pin_3, S3.Pin_4, S4.Pin_3, S4.Pin_4, Part1.3.3V, S5.Pin_3, S5.Pin_4, S6.Pin_3, S6.Pin_4
  N3: S2.Pin_1, S2.Pin_2, D6.anode, D7.anode
  N4: S3.Pin_1, S3.Pin_2, D8.anode, D11.anode
  N5: S4.Pin_1, S4.Pin_2, D3.anode, D12.anode
  N6: Part1.GND, R1.Pin_0, R2.Pin_0, R3.Pin_0, R4.Pin_0, R5.Pin_1
  N7: Part1.GPIO0, R4.Pin_1, D8.cathode, D9.cathode, D12.cathode
  N8: Part1.GPIO16, R5.Pin_0, D1.cathode, D7.cathode, D10.cathode
  N9: Part1.GPIO2, R1.Pin_1, D4.cathode, D11.cathode
  N10: Part1.GPIO5/SCL, R2.Pin_1, D2.cathode, D5.cathode
  N11: Part1.GPIO4/SDA, R3.Pin_1, D3.cathode, D6.cathode
  N12: S5.Pin_1, S5.Pin_2, D1.anode, D5.anode
  N13: S6.Pin_1, S6.Pin_2, D2.anode, D9.anode

custom parts:
  Adafruit Feather HUZZAH ESP8266: his is the Adafruit Feather HUZZAH ESP8266 - our take on an 'all-in-one' ESP8266 WiFi development board with built in USB and battery charging. Its an ESP8266 WiFi module with all the extras you need, ready to rock! We have other boards in the Feather family, check'em out here. At the Feather HUZZAH's heart is an ESP8266 WiFi microcontroller clocked at 80 MHz and at 3.3V logic. This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
