# Fritzing sketch 2x3-keypad-matrix-wiring (saved by Fritzing 0.9.3b)
breadboards: 2

parts:
  S1 = Pushbutton [package="[THT]"]
  S2 = Pushbutton [package="[THT]"]
  S3 = Pushbutton [package="[THT]"]
  S4 = Pushbutton [package="[THT]"]
  Part1 = Adafruit Feather HUZZAH ESP8266 [part_number="Adafruit #2821"]
  S5 = Pushbutton [package="[THT]"]
  S6 = Pushbutton [package="[THT]"]

nets:
  N1: S1.Pin_1, S1.Pin_2, S3.Pin_1, S3.Pin_2, Part1.GPIO4/SDA
  N2: S1.Pin_3, S1.Pin_4, S2.Pin_3, S2.Pin_4, Part1.GPIO16, S5.Pin_3, S5.Pin_4
  N3: S2.Pin_1, S2.Pin_2, S4.Pin_1, S4.Pin_2, Part1.GPIO2
  N4: S3.Pin_3, S3.Pin_4, S4.Pin_3, S4.Pin_4, Part1.GPIO0, S6.Pin_3, S6.Pin_4
  N5: Part1.GPIO5/SCL, S5.Pin_1, S5.Pin_2, S6.Pin_1, S6.Pin_2

custom parts:
  Adafruit Feather HUZZAH ESP8266: his is the Adafruit Feather HUZZAH ESP8266 - our take on an 'all-in-one' ESP8266 WiFi development board with built in USB and battery charging. Its an ESP8266 WiFi module with all the extras you need, ready to rock! We have other boards in the Feather family, check'em out here. At the Feather HUZZAH's heart is an ESP8266 WiFi microcontroller clocked at 80 MHz and at 3.3V logic. This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
